// Logisim project nand2tetris.circ as structural Verilog
module nand2logic (
  input  [15:0] in_1,
  input  [15:0] in_2,
  input  in_3,
  input  [1:0] in_4,
  input  in_5,
  input  in_6,
  input  in_7,
  input  in_8,
  input  in_9,
  input  in_10,
  input  A,
  input  B,
  input  SEL,
  input  in_14,
  input  in_15,
  output out_16,
  output out_17,
  output out_18,
  output out_19,
  output out_20,
  output O,
  output out_22,
  output out_23
);

  wire and_1_out, nand_2_out, nand_3_out, nand_4_out, nand_5_out, nand_6_out, nand_7_out, nand_10_out,
       nand_11_out, nand_12_out, nand_13_out, nand_14_out, nand_15_out, nand_16_out, not_1_out, not_2_out,
       or8way_1_out_2, or8way_2_out_2, or_2_out;
  wire [15:0] or_1_out;

  nand nand_1 (out_17, in_3, in_3);
  nand nand_2 (nand_2_out, in_5, in_6);
  nand nand_3 (nand_3_out, in_7, in_7);
  nand nand_4 (nand_4_out, in_8, in_8);
  nand nand_5 (nand_5_out, in_9, in_9);
  nand nand_6 (nand_6_out, in_10, in_10);
  nand nand_7 (nand_7_out, SEL, SEL);
  nand nand_8 (out_18, nand_2_out, nand_2_out);
  nand nand_9 (out_19, nand_3_out, nand_4_out);
  nand nand_10 (nand_10_out, A, nand_7_out);
  nand nand_11 (nand_11_out, B, SEL);
  nand nand_12 (nand_12_out, in_14, nand_13_out);
  nand nand_13 (nand_13_out, in_15, in_15);
  nand nand_14 (nand_14_out, in_14, in_15);
  nand nand_15 (nand_15_out, in_10, nand_5_out);
  nand nand_16 (nand_16_out, nand_6_out, in_9);
  nand nand_17 (out_22, nand_12_out, nand_12_out);
  nand nand_18 (out_23, nand_14_out, nand_14_out);
  nand nand_19 (out_20, nand_15_out, nand_16_out);
  nand nand_20 (O, nand_10_out, nand_11_out);
  Mux16 mux16_1 ();  // open: A, B, SEL, O
  Mux4Way16 mux4way16_1 ();  // open: A, B, C, D, SEL, O
  assign or_1_out = in_1 | in_2;  // OR_Gate or_1, 16 bits wide
  not not_1 (not_1_out, in_4[0]);
  not not_2 (not_2_out, in_4[1]);
  and and_1 (and_1_out, not_1_out, not_2_out);
  and and_2 (out_16, or_2_out, and_1_out);
  Or8Way or8way_1 (.I(or_1_out[7:0]), .out_2(or8way_1_out_2));
  Or8Way or8way_2 (.I(or_1_out[15:8]), .out_2(or8way_2_out_2));
  or or_2 (or_2_out, or8way_1_out_2, or8way_2_out_2);

  // Notes on the sheet:
  //   NOT
  //   AND
  //   OR
  //   XOR
  //   DMux
  //   Mux
endmodule

module Mux16 (
  input  [15:0] A,
  input  [15:0] B,
  input  SEL,
  output [15:0] O
);

  wire not_1_out;

  assign O = not_1_out ? A : 16'bz;  // Controlled_Buffer controlled_buffer_1
  not not_1 (not_1_out, SEL);
  assign O = SEL ? B : 16'bz;  // Controlled_Buffer controlled_buffer_2
endmodule

module Or8Way (
  input  [7:0] I,
  output out_2
);

  wire or_1_out, or_2_out, or_3_out, or_4_out, or_5_out, or_6_out;

  or or_1 (or_1_out, I[0], I[1]);
  or or_2 (or_2_out, or_1_out, I[2]);
  or or_3 (or_3_out, or_2_out, I[3]);
  or or_4 (or_4_out, or_3_out, I[4]);
  or or_5 (or_5_out, or_4_out, I[5]);
  or or_6 (or_6_out, or_5_out, I[6]);
  or or_7 (out_2, or_6_out, I[7]);
endmodule

module Mux4Way16 (
  input  [15:0] A,
  input  [15:0] B,
  input  [15:0] C,
  input  [15:0] D,
  input  [1:0] SEL,
  output [15:0] O
);

  wire [15:0] mux16_1_o, mux16_2_o;

  Mux16 mux16_1 (.A(A), .B(B), .SEL(SEL[0]), .O(mux16_1_o));
  Mux16 mux16_2 (.A(C), .B(D), .SEL(SEL[0]), .O(mux16_2_o));
  Mux16 mux16_3 (.A(mux16_1_o), .B(mux16_2_o), .SEL(SEL[1]), .O(O));
endmodule

module Mux8Way16 (
  input  [3:0] SEL,
  input  [15:0] A,
  input  [15:0] B,
  input  [15:0] C,
  input  [15:0] D,
  input  [15:0] E,
  input  [15:0] F,
  input  [15:0] G,
  input  [15:0] H,
  output [15:0] out_10
);

  wire [15:0] mux4way16_1_o, mux4way16_2_o;

  Mux4Way16 mux4way16_1 (.A(A), .B(B), .C(C), .D(D), .SEL(SEL[1:0]), .O(mux4way16_1_o));
  Mux4Way16 mux4way16_2 (.A(E), .B(F), .C(G), .D(H), .SEL(SEL[1:0]), .O(mux4way16_2_o));
  Mux16 mux16_1 (.A(mux4way16_1_o), .B(mux4way16_2_o), .SEL(SEL[2]), .O(out_10));
endmodule

module DMux4Way (
  input  I,
  input  [1:0] SEL,
  output A,
  output B,
  output C,
  output D
);

  wire and_1_out, and_2_out, and_3_out, and_4_out, not_1_out, not_2_out, not_3_out, not_4_out, undriven;

  not not_1 (not_1_out, SEL[0]);
  and and_1 (and_1_out, not_1_out, not_2_out);
  not not_2 (not_2_out, SEL[1]);
  and and_2 (and_2_out, SEL[0], not_3_out);
  not not_3 (not_3_out, SEL[1]);
  and and_3 (and_3_out, SEL[1], not_4_out);
  not not_4 (not_4_out, SEL[0]);
  and and_4 (and_4_out, SEL[0], SEL[1]);
  and and_5 (A, I, and_1_out);
  and and_6 (B, I, and_2_out);
  and and_7 (C, I, and_3_out);
  and and_8 (D, I, and_4_out);
  // NAND_Gate nand_1 has open pins: in0=undriven, in1=undriven, out=open
endmodule

module DMux8Way (
  input  I,
  input  [3:0] SEL,
  output A,
  output B,
  output C,
  output D,
  output E,
  output F,
  output G,
  output H
);

  wire and_1_out, and_2_out, not_1_out;

  and and_1 (and_1_out, I, not_1_out);
  not not_1 (not_1_out, SEL[2]);
  and and_2 (and_2_out, I, SEL[2]);
  DMux4Way dmux4way_1 (.I(and_1_out), .SEL(SEL[1:0]), .A(A), .B(B), .C(C), .D(D));
  DMux4Way dmux4way_2 (.I(and_2_out), .SEL(SEL[1:0]), .A(E), .B(F), .C(G), .D(H));
endmodule

module DMux (
  input  I,
  input  SEL,
  output O1,
  output O2
);

  wire nand_1_out, nand_2_out, nand_3_out;

  nand nand_1 (nand_1_out, SEL, SEL);
  nand nand_2 (nand_2_out, I, nand_1_out);
  nand nand_3 (nand_3_out, I, SEL);
  nand nand_4 (O1, nand_2_out, nand_2_out);
  nand nand_5 (O2, nand_3_out, nand_3_out);
endmodule

module FullAdder (
  input  I,
  input  A,
  input  B,
  output S,
  output C
);

  wire and_1_out, and_2_out, xor_1_out;

  and and_1 (and_1_out, A, B);
  xor xor_1 (xor_1_out, A, B);
  and and_2 (and_2_out, xor_1_out, I);
  or or_1 (C, and_1_out, and_2_out);
  xor xor_2 (S, I, xor_1_out);
endmodule

module Add16 (
  input  [15:0] A,
  input  [15:0] B,
  output [15:0] S
);

  wire fulladder_1_c, fulladder_2_c, fulladder_3_c, fulladder_4_c, fulladder_5_c, fulladder_6_c,
       fulladder_7_c, fulladder_8_c, fulladder_9_c, fulladder_10_c, fulladder_11_c, fulladder_12_c,
       fulladder_13_c, fulladder_14_c, fulladder_15_c;

  FullAdder fulladder_1 (.A(A[0]), .B(B[0]), .S(S[0]), .C(fulladder_1_c));  // open: I
  FullAdder fulladder_2 (.I(fulladder_1_c), .A(A[1]), .B(B[1]), .S(S[1]), .C(fulladder_2_c));
  FullAdder fulladder_3 (.I(fulladder_2_c), .A(A[2]), .B(B[2]), .S(S[2]), .C(fulladder_3_c));
  FullAdder fulladder_4 (.I(fulladder_3_c), .A(A[3]), .B(B[3]), .S(S[3]), .C(fulladder_4_c));
  FullAdder fulladder_5 (.I(fulladder_4_c), .A(A[4]), .B(B[4]), .S(S[4]), .C(fulladder_5_c));
  FullAdder fulladder_6 (.I(fulladder_5_c), .A(A[5]), .B(B[5]), .S(S[5]), .C(fulladder_6_c));
  FullAdder fulladder_7 (.I(fulladder_6_c), .A(A[6]), .B(B[6]), .S(S[6]), .C(fulladder_7_c));
  FullAdder fulladder_8 (.I(fulladder_7_c), .A(A[7]), .B(B[7]), .S(S[7]), .C(fulladder_8_c));
  FullAdder fulladder_9 (.I(fulladder_8_c), .A(A[8]), .B(B[8]), .S(S[8]), .C(fulladder_9_c));
  FullAdder fulladder_10 (.I(fulladder_9_c), .A(A[9]), .B(B[9]), .S(S[9]), .C(fulladder_10_c));
  FullAdder fulladder_11 (.I(fulladder_10_c), .A(A[10]), .B(B[10]), .S(S[10]), .C(fulladder_11_c));
  FullAdder fulladder_12 (.I(fulladder_11_c), .A(A[11]), .B(B[11]), .S(S[11]), .C(fulladder_12_c));
  FullAdder fulladder_13 (.I(fulladder_12_c), .A(A[12]), .B(B[12]), .S(S[12]), .C(fulladder_13_c));
  FullAdder fulladder_14 (.I(fulladder_13_c), .A(A[13]), .B(B[13]), .S(S[13]), .C(fulladder_14_c));
  FullAdder fulladder_15 (.I(fulladder_14_c), .A(A[14]), .B(B[14]), .S(S[14]), .C(fulladder_15_c));
  FullAdder fulladder_16 (.I(fulladder_15_c), .A(A[15]), .B(B[15]), .S(S[15]));  // open: C
endmodule

module Inc16 (
  input  [15:0] I,
  output [15:0] O
);

  Add16 add16_1 (.A(I), .B(16'h1), .S(O));
endmodule

module ALU16 (
  input  [15:0] A,
  input  [15:0] B,
  input  ZX,
  input  NX,
  input  ZY,
  input  NY,
  input  F,
  input  NO,
  output [15:0] O,
  output ZR,
  output NG
);

  wire or16way_1_o;
  wire [15:0] add16_1_s, and_1_out, mux4way16_1_o, mux4way16_2_o, mux16_2_o, not_1_out, not_2_out, not_3_out;

  assign not_1_out = ~A;  // NOT_Gate not_1, 16 bits wide
  assign not_2_out = ~B;  // NOT_Gate not_2, 16 bits wide
  Mux4Way16 mux4way16_1 (.A(A), .B({16{1'b0}}), .C(not_1_out), .D({16{1'b1}}), .SEL({NX, ZX}), .O(mux4way16_1_o));
  Mux4Way16 mux4way16_2 (.A(B), .B({16{1'b0}}), .C(not_2_out), .D({16{1'b1}}), .SEL({NY, ZY}), .O(mux4way16_2_o));
  assign not_3_out = ~mux16_2_o;  // NOT_Gate not_3, 16 bits wide
  assign and_1_out = mux4way16_1_o & mux4way16_2_o;  // AND_Gate and_1, 16 bits wide
  Add16 add16_1 (.A(mux4way16_1_o), .B(mux4way16_2_o), .S(add16_1_s));
  Mux16 mux16_1 (.A(mux16_2_o), .B(not_3_out), .SEL(NO), .O({NG, O[14:0]}));
  Mux16 mux16_2 (.A(and_1_out), .B(add16_1_s), .SEL(F), .O(mux16_2_o));
  Or16Way or16way_1 (.I({NG, O[14:0]}), .O(or16way_1_o));
  not not_4 (ZR, or16way_1_o);

  assign O[15] = NG;
endmodule

module Or16Way (
  input  [15:0] I,
  output O
);

  wire or8way_1_out_2, or8way_2_out_2;

  Or8Way or8way_1 (.I(I[7:0]), .out_2(or8way_1_out_2));
  Or8Way or8way_2 (.I(I[15:8]), .out_2(or8way_2_out_2));
  or or_1 (O, or8way_1_out_2, or8way_2_out_2);
endmodule

module Bit (
  input  I,
  input  LD,
  output O
);

  wire and_1_out, and_2_out, nor_1_out, not_1_out;

  not not_1 (not_1_out, I);
  and and_1 (and_1_out, I, LD);
  and and_2 (and_2_out, LD, not_1_out);
  nor nor_1 (nor_1_out, and_1_out, O);
  nor nor_2 (O, nor_1_out, and_2_out);
endmodule

module Register16 (
  input  [15:0] I,
  input  LD,
  output [15:0] O
);

  Bit bit_1 (.I(I[0]), .LD(LD), .O(O[0]));
  Bit bit_2 (.I(I[1]), .LD(LD), .O(O[1]));
  Bit bit_3 (.I(I[2]), .LD(LD), .O(O[2]));
  Bit bit_4 (.I(I[3]), .LD(LD), .O(O[3]));
  Bit bit_5 (.I(I[4]), .LD(LD), .O(O[4]));
  Bit bit_6 (.I(I[5]), .LD(LD), .O(O[5]));
  Bit bit_7 (.I(I[6]), .LD(LD), .O(O[6]));
  Bit bit_8 (.I(I[7]), .LD(LD), .O(O[7]));
  Bit bit_9 (.I(I[8]), .LD(LD), .O(O[8]));
  Bit bit_10 (.I(I[9]), .LD(LD), .O(O[9]));
  Bit bit_11 (.I(I[10]), .LD(LD), .O(O[10]));
  Bit bit_12 (.I(I[11]), .LD(LD), .O(O[11]));
  Bit bit_13 (.I(I[12]), .LD(LD), .O(O[12]));
  Bit bit_14 (.I(I[13]), .LD(LD), .O(O[13]));
  Bit bit_15 (.I(I[14]), .LD(LD), .O(O[14]));
  Bit bit_16 (.I(I[15]), .LD(LD), .O(O[15]));
endmodule

module RAM8 (
  input  [15:0] I,
  input  [3:0] ADDR,
  input  LD,
  output [15:0] out_4
);

  wire dmux8way_1_a, dmux8way_1_b, dmux8way_1_c, dmux8way_1_d, dmux8way_1_e, dmux8way_1_f, dmux8way_1_g,
       dmux8way_1_h;
  wire [15:0] register16_1_o, register16_2_o, register16_3_o, register16_4_o, register16_5_o, register16_6_o,
       register16_7_o, register16_8_o;

  DMux8Way dmux8way_1 (
    .I(LD), .SEL(ADDR), .A(dmux8way_1_a), .B(dmux8way_1_b), .C(dmux8way_1_c), .D(dmux8way_1_d),
    .E(dmux8way_1_e), .F(dmux8way_1_f), .G(dmux8way_1_g), .H(dmux8way_1_h));
  Register16 register16_1 (.I(I), .LD(dmux8way_1_a), .O(register16_1_o));
  Register16 register16_2 (.I(I), .LD(dmux8way_1_b), .O(register16_2_o));
  Register16 register16_3 (.I(I), .LD(dmux8way_1_c), .O(register16_3_o));
  Register16 register16_4 (.I(I), .LD(dmux8way_1_d), .O(register16_4_o));
  Register16 register16_5 (.I(I), .LD(dmux8way_1_e), .O(register16_5_o));
  Register16 register16_6 (.I(I), .LD(dmux8way_1_f), .O(register16_6_o));
  Register16 register16_7 (.I(I), .LD(dmux8way_1_g), .O(register16_7_o));
  Register16 register16_8 (.I(I), .LD(dmux8way_1_h), .O(register16_8_o));
  Mux8Way16 mux8way16_1 (
    .SEL(ADDR), .A(register16_1_o), .B(register16_2_o), .C(register16_3_o), .D(register16_4_o),
    .E(register16_5_o), .F(register16_6_o), .G(register16_7_o), .H(register16_8_o), .out_10(out_4));
endmodule

module RAM64 (
  input  [15:0] I,
  input  [6:0] ADDR,
  input  LD,
  output [15:0] O
);

  wire dmux8way_1_a, dmux8way_1_b, dmux8way_1_c, dmux8way_1_d, dmux8way_1_e, dmux8way_1_f, dmux8way_1_g;
  wire [15:0] ram8_1_out_4, ram8_2_out_4, ram8_3_out_4, ram8_4_out_4, ram8_5_out_4, ram8_6_out_4,
       ram8_7_out_4, ram8_8_out_4;

  DMux8Way dmux8way_1 (
    .I(LD), .SEL({1'b0, ADDR[6:4]}), .A(dmux8way_1_a), .B(dmux8way_1_b), .C(dmux8way_1_c), .D(dmux8way_1_d),
    .E(dmux8way_1_e), .F(dmux8way_1_f), .G(dmux8way_1_g));  // open: H
  RAM8 ram8_1 (.I(I), .ADDR(ADDR[3:0]), .LD(dmux8way_1_a), .out_4(ram8_1_out_4));
  RAM8 ram8_2 (.I(I), .ADDR(ADDR[3:0]), .LD(dmux8way_1_b), .out_4(ram8_2_out_4));
  RAM8 ram8_3 (.I(I), .ADDR(ADDR[3:0]), .LD(dmux8way_1_c), .out_4(ram8_3_out_4));
  RAM8 ram8_4 (.I(I), .ADDR(ADDR[3:0]), .LD(dmux8way_1_d), .out_4(ram8_4_out_4));
  RAM8 ram8_5 (.I(I), .ADDR(ADDR[3:0]), .LD(dmux8way_1_e), .out_4(ram8_5_out_4));
  RAM8 ram8_6 (.I(I), .ADDR(ADDR[3:0]), .out_4(ram8_6_out_4));  // open: LD
  RAM8 ram8_7 (.I(I), .ADDR(ADDR[3:0]), .LD(dmux8way_1_f), .out_4(ram8_7_out_4));
  RAM8 ram8_8 (.I(I), .ADDR(ADDR[3:0]), .LD(dmux8way_1_g), .out_4(ram8_8_out_4));
  Mux8Way16 mux8way16_1 (
    .SEL({1'b0, ADDR[6:4]}), .A(ram8_1_out_4), .B(ram8_2_out_4), .C(ram8_3_out_4), .D(ram8_4_out_4),
    .E(ram8_5_out_4), .F(ram8_6_out_4), .G(ram8_7_out_4), .H(ram8_8_out_4), .out_10(O));
endmodule

module RAM512 (
  input  [15:0] I,
  input  [9:0] ADDR,
  input  LD,
  output [15:0] O
);

  wire dmux8way_1_a, dmux8way_1_b, dmux8way_1_c, dmux8way_1_d, dmux8way_1_e, dmux8way_1_f, dmux8way_1_g,
       dmux8way_1_h;
  wire [15:0] ram64_1_o, ram64_2_o, ram64_3_o, ram64_4_o, ram64_5_o, ram64_6_o, ram64_7_o, ram64_8_o;

  DMux8Way dmux8way_1 (
    .I(LD), .SEL({1'b0, ADDR[9:7]}), .A(dmux8way_1_a), .B(dmux8way_1_b), .C(dmux8way_1_c), .D(dmux8way_1_d),
    .E(dmux8way_1_e), .F(dmux8way_1_f), .G(dmux8way_1_g), .H(dmux8way_1_h));
  RAM64 ram64_1 (.I(I), .ADDR(ADDR[6:0]), .LD(dmux8way_1_a), .O(ram64_1_o));
  RAM64 ram64_2 (.I(I), .ADDR(ADDR[6:0]), .LD(dmux8way_1_b), .O(ram64_2_o));
  RAM64 ram64_3 (.I(I), .ADDR(ADDR[6:0]), .LD(dmux8way_1_c), .O(ram64_3_o));
  RAM64 ram64_4 (.I(I), .ADDR(ADDR[6:0]), .LD(dmux8way_1_d), .O(ram64_4_o));
  RAM64 ram64_5 (.I(I), .ADDR(ADDR[6:0]), .LD(dmux8way_1_e), .O(ram64_5_o));
  RAM64 ram64_6 (.I(I), .ADDR(ADDR[6:0]), .LD(dmux8way_1_f), .O(ram64_6_o));
  RAM64 ram64_7 (.I(I), .ADDR(ADDR[6:0]), .LD(dmux8way_1_g), .O(ram64_7_o));
  RAM64 ram64_8 (.I(I), .ADDR(ADDR[6:0]), .LD(dmux8way_1_h), .O(ram64_8_o));
  Mux8Way16 mux8way16_1 (
    .SEL({1'b0, ADDR[9:7]}), .A(ram64_1_o), .B(ram64_2_o), .C(ram64_3_o), .D(ram64_4_o), .E(ram64_5_o),
    .F(ram64_6_o), .G(ram64_7_o), .H(ram64_8_o), .out_10(O));
endmodule

module PC (
  input  [15:0] I,
  input  RST,
  input  LD,
  input  INC,
  output [15:0] O
);

  wire or_1_out;
  wire [15:0] inc16_1_o, mux16_1_o, mux16_2_o, mux16_3_o;

  or or_1 (or_1_out, LD, RST, INC);
  Inc16 inc16_1 (.I(O), .O(inc16_1_o));
  Mux16 mux16_1 (.A(mux16_2_o), .B(I), .SEL(LD), .O(mux16_1_o));
  Mux16 mux16_2 (.A({16{1'b0}}), .B(inc16_1_o), .SEL(INC), .O(mux16_2_o));
  Mux16 mux16_3 (.A(mux16_1_o), .B({16{1'b0}}), .SEL(RST), .O(mux16_3_o));
  Register16 register16_1 (.I(mux16_3_o), .LD(or_1_out), .O(O));
endmodule

module CPU (
  input  [15:0] instruction,
  input  [15:0] inM,
  input  RST,
  output [15:0] outM,
  output wM,
  output [14:0] addrM,
  output [14:0] progC
);

  wire alu16_1_ng, alu16_1_zr, and_2_out, and_3_out, and_4_out, and_5_out, nor_1_out, not_1_out, not_2_out,
       or_1_out, or_2_out;
  wire [15:0] dRegister_o, mux16_1_o, mux16_2_o;
  wire [15:15] aRegister_o, pc_1_o;

  and and_1 (wM, instruction[3], instruction[15]);
  and and_2 (and_2_out, alu16_1_ng, instruction[2]);
  and and_3 (and_3_out, instruction[0], nor_1_out);
  nor nor_1 (nor_1_out, alu16_1_zr, alu16_1_ng);
  and and_4 (and_4_out, alu16_1_zr, instruction[1]);
  and and_5 (and_5_out, instruction[15], or_1_out);
  or or_1 (or_1_out, and_2_out, and_3_out, and_4_out);
  not not_1 (not_1_out, and_5_out);
  Mux16 mux16_1 (.A(instruction), .B(outM), .SEL(instruction[15]), .O(mux16_1_o));
  or or_2 (or_2_out, not_2_out, instruction[5]);
  not not_2 (not_2_out, instruction[15]);
  PC pc_1 (.I({aRegister_o[15], addrM}), .RST(RST), .LD(and_5_out), .INC(not_1_out), .O({pc_1_o[15], progC}));
  Register16 aRegister (.I(mux16_1_o), .LD(or_2_out), .O({aRegister_o[15], addrM}));
  Mux16 mux16_2 (.A({aRegister_o[15], addrM}), .B(inM), .SEL(instruction[12]), .O(mux16_2_o));
  Register16 dRegister (.I(outM), .LD(instruction[4]), .O(dRegister_o));
  ALU16 alu16_1 (
    .A(dRegister_o), .B(mux16_2_o), .ZX(instruction[11]), .NX(instruction[10]), .ZY(instruction[9]),
    .NY(instruction[8]), .F(instruction[7]), .NO(instruction[6]), .O(outM), .ZR(alu16_1_zr), .NG(alu16_1_ng));
endmodule

module Memory (
  input  [15:0] I,
  input  [14:0] ADDR,
  input  LD,
  input  kbdLD,
  output [15:0] O,
  output [15:0] scrnO,
  output [15:0] kbdO
);

  wire dmux_1_o1, dmux_1_o2;
  wire [15:0] ram_1_dout;

  DMux dmux_1 (.I(LD), .SEL(ADDR[14]), .O1(dmux_1_o1), .O2(dmux_1_o2));
  RAM #(.addrWidth(14), .dataWidth(16), .trigger("high")) ram_1 (
    .addr(ADDR[13:0]), .we(dmux_1_o1), .oe(1'b1), .din(I), .dout(ram_1_dout));
  RAM #(.addrWidth(13), .dataWidth(16), .trigger("high")) ram_2 (
    .we(dmux_1_o2), .oe(1'b1), .din(I), .dout(scrnO));  // open: addr
  Register16 register16_1 (.I(I), .LD(kbdLD), .O(kbdO));
  Mux4Way16 mux4way16_1 (.A(ram_1_dout), .B(ram_1_dout), .C(scrnO), .D(kbdO), .SEL(ADDR[14:13]), .O(O));
endmodule

module Computer (
  input  RST
);

  wire cpu_1_wm;
  wire [14:0] cpu_1_addrm, cpu_1_progc;
  wire [15:0] cpu_1_outm, memory_1_o, rom_1_data;

  ROM #(.addrWidth(15), .dataWidth(16)) rom_1 (.addr(cpu_1_progc), .data(rom_1_data));
  CPU cpu_1 (
    .instruction(rom_1_data), .inM(memory_1_o), .RST(RST), .outM(cpu_1_outm), .wM(cpu_1_wm),
    .addrM(cpu_1_addrm), .progC(cpu_1_progc));
  Memory memory_1 (.I(cpu_1_outm), .ADDR(cpu_1_addrm), .LD(cpu_1_wm), .O(memory_1_o));  // open: kbdLD, scrnO, kbdO

  // Notes on the sheet:
  //   contents of rom_1 (hex, n*v repeats v):
  //   1
endmodule
